// Logisim project Adder.circ as structural Verilog: 2 circuits, main circuit main
module main (
  input  A,
  input  B,
  input  CIN,
  output SUM,
  output COUT
);

  wire and_1_out, and_2_out, xor_1_out;

  xor xor_1 (xor_1_out, A, B);
  xor xor_2 (SUM, xor_1_out, CIN);
  and and_1 (and_1_out, CIN, xor_1_out);
  and and_2 (and_2_out, A, B);
  or or_1 (COUT, and_1_out, and_2_out);
endmodule

module FULL_ADDER (
  input  A0,
  input  B0,
  input  Cin,
  output Cout,
  output sum
);

  main FULL_ADDER (.A(A0), .B(B0), .CIN(Cin), .SUM(sum), .COUT(Cout));
endmodule
