// Logisim project comprator.circ as structural Verilog: 2 circuits, main circuit main
module main (
  input  A,
  input  B,
  output A___B,
  output A___B_2,
  output A___B_3
);

  wire not_1_out, not_2_out;

  not not_1 (not_1_out, B);
  not not_2 (not_2_out, A);
  and and_1 (A___B, A, not_1_out);
  xnor xnor_1 (A___B_2, A, B);
  and and_2 (A___B_3, not_2_out, B);
endmodule

module COMPARATOR (
  input  in_1,
  input  in_2,
  output out_3,
  output out_4,
  output out_5
);

  main COMPARATOR (.A(in_1), .B(in_2), .A___B(out_3), .A___B_2(out_4), .A___B_3(out_5));
endmodule
