// Logisim project fulladder.circ as structural Verilog: 2 circuits, main circuit mult
module mult (
  input  in_1,
  input  in_2,
  input  in_3,
  output out_4
);

  wire nand_1_out, nand_2_out, nand_3_out;

  nand nand_1 (nand_1_out, in_2, in_2);
  nand nand_2 (nand_2_out, in_1, in_2);
  nand nand_3 (nand_3_out, nand_1_out, in_3);
  nand nand_4 (out_4, nand_2_out, nand_3_out);
endmodule

module top (
  input  in_1,
  input  in_2,
  input  in_3,
  output out_4,
  output out_5
);

  wire and_1_out, and_2_out, xor_1_out, xor_2_out;

  ExactlyOne xor_1 (.out(xor_1_out), .in0(in_1), .in1(in_1), .in2(in_1), .in3(in_1), .in4(in_1));
  xor xor_2 (xor_2_out, xor_1_out, in_3);
  and and_1 (and_1_out, in_3, xor_1_out);
  buf and_2 (and_2_out, in_1);  // AND_Gate
  // OR_Gate or_1 has open pins: out=out_5

  assign in_2 = in_1;
endmodule
