// Logisim project halfadder.circ as structural Verilog: 1 circuit, main circuit main
module main (
  input  A,
  input  B,
  output out_3,
  output out_4
);

  and and_1 (out_3, A, B);
  xor xor_1 (out_4, A, B);
endmodule
