// Logisim project mux.circ as structural Verilog: 2 circuits, main circuit main
module main (
  input  in_1,
  input  in_2,
  input  in_3,
  output out_4
);

  wire nand_1_out, nand_2_out, nand_3_out;

  nand nand_1 (nand_1_out, in_1, in_2);
  nand nand_2 (nand_2_out, in_2, in_2);
  nand nand_3 (nand_3_out, nand_2_out, in_3);
  nand nand_4 (out_4, nand_1_out, nand_3_out);
endmodule

module MUX (
  input  in_1,
  input  in_2,
  input  in_3
);

  wire main_1_out_4;

  main main_1 (.in_1(in_1), .in_2(in_3), .in_3(in_2), .out_4(main_1_out_4));
  LED led_1 (.in(main_1_out_4));
endmodule
